# Fritzing sketch GateKeeperCircuit (saved by Fritzing 0.9.10b)

parts:
  Raspberry_Pi_1 = Raspberry Pi 3 [part_number=RPI-3-V1.2]
  Part1 = Arduino Nano (Rev3.0)
  J1 = Basic Servo
  J2 = Basic Servo
  J3 = Basic Servo
  J4 = Basic Servo
  J5 = Basic Servo
  J6 = Basic Servo
  J7 = Basic Servo
  J8 = Basic Servo
  Q1 = Basic FET N-Channel [package="DPak [SMD]"]
  Q2 = Basic FET N-Channel [package="DPak [SMD]"]
  Q3 = Basic FET N-Channel [package="DPak [SMD]"]
  Q4 = Basic FET N-Channel [package="DPak [SMD]"]
  U1 = LIPO-2000mAh [package=lipo-2000]  # not connected
  U2 = LIPO-2000mAh [package=lipo-2000]  # not connected

nets:
  N1: Raspberry_Pi_1.GIPO15, Part1.D1/TX
  N2: Raspberry_Pi_1.GIPO14, Part1.D0/RX
  N3: Part1.D2, Q4.Gate
  N4: Part1.D3, Q3.Gate
  N5: Part1.D4, Q2.Gate
  N6: Part1.D5, Q1.Gate
  N7: Part1.D6, J4.pulse
  N8: Part1.D7, J3.pulse
  N9: Part1.D8, J6.pulse
  N10: Part1.D9, J5.pulse
  N11: Part1.D10, J7.pulse
  N12: Part1.D11/MOSI, J1.pulse
  N13: Part1.D12/MISO, J2.pulse
  N14: Part1.A0, J8.pulse
  N15: J2.gnd, Q1.drain
  N16: J4.gnd, Q2.drain
  N17: J6.gnd, Q3.drain
  N18: J8.gnd, Q4.drain
